# Fritzing sketch Conveyor stepper motor diagram (saved by Fritzing 0.9.3b)
breadboards: 1

parts:
  A1 = TB6600 NEMA-17-23 STEPPER MOTOR DRIVER [package=THT]
  M1 = Stepper Motor - Bipolar
  J1 = STM32 Nucleo boards
  Part2 = Breadboard Power Supply Board SMD
  J3 = Power Jack [package=power_jack_smd]
  Keypad4x1 = Keypad Membran 4x4

nets:
  N1: A1.Pin_1, J3.GNDBREAK
  N2: A1.Pin_2, J3.GND
  N3: A1.Pin_3, M1.D
  N4: A1.Pin_4, M1.B
  N5: A1.Pin_5, M1.C
  N6: A1.Pin_6, M1.A
  N7: A1.Pin_7, J1.D7
  GND: A1.Pin_8, A1.Pin_10, A1.Pin_11, A1.Pin_12, J1.GND, Part2.GND
  N8: A1.Pin_9, J1.D6_PWM
  N9: J1.PB11, Keypad4x1.Pin6
  N10: J1.A4/SDA, Keypad4x1.Pin4
  N11: J1.A5/SCL, Keypad4x1.Pin5
  N12: J1.D4, Keypad4x1.Pin1
  N13: J1.D5_PWM, Keypad4x1.Pin2
  VIN: J1.VIN, Part2.VCC
  N14: J1.PB2, Keypad4x1.Pin8
  N15: J1.PB1, Keypad4x1.Pin7
  N16: J1.PB7, Keypad4x1.Pin3

notes:
  24V 5A Power Supply

custom parts:
  TB6600 NEMA-17-23 STEPPER MOTOR DRIVER: cheap Nema-17-23 steppermotor driver board
  Keypad Membran 4x4: Membrane Keypad 4x4 Matrix
