# Fritzing sketch pixycam (saved by Fritzing 0.9.3b)
breadboards: 1

parts:
  U1 = TRANSCHIPTC5747 [package=camera_sfv24r-2st_2]
  J1 = STM32 Nucleo boards
  Part3 = Breadboard Power Supply Board SMD

nets:
  VIN: U1.SCLK, J1.VIN, Part3.VCC
  GND: U1.AGND, J1.GND, Part3.GND
  N1: U1.DOUT_2, J1.PB15
  N2: U1.DOUT_3, J1.PB14
  N3: U1.DOUT_4, J1.PB13
  N4: U1.DOUT_5, J1.PB12

notes:
  PixyCam to STM32
  SPI2_MOSI to PB15
  SPI_MISO to PB14
  SPI2_SCK to PB13
  SPI2_NSS to PB12
  5v, GND
